# Fritzing sketch RobotProto (saved by Fritzing 0.9.3b)
circuit board: 11.5592cm x 10.7442cm
breadboards: 1

parts:
  MD03A1 = Dual VNH2SP30 Motor Driver [part_number=MD03A]
  MD03A2 = Dual VNH2SP30 Motor Driver [part_number=MD03A]
  DC_Mot_Enc1 = DC Motor with two-phase hall-encoder [part_number=VT-E-G25A-06-177E]
  DC_Mot_Enc2 = DC Motor with two-phase hall-encoder [part_number=VT-E-G25A-06-177E]
  Part2 = NRF24L01+ Breakout Board
  DC_Mot_Enc5 = DC Motor with two-phase hall-encoder [part_number=VT-E-G25A-06-177E]
  VCC1 = 4 x AAA Battery Mount
  U1 = GAS_SENSOR [package=mq-3]
  Part1 = Arduino Mega 2560 (Rev3)
  J1 = Basic Servo

nets:
  N1: MD03A1.1INa, Part1.D7_PWM
  N2: MD03A1.1INb, Part1.D9_PWM
  N3: MD03A1.PWM, Part1.D30
  GND: MD03A1.GND#136, MD03A1.GND#138, MD03A2.GND#136, MD03A2.GND#138, DC_Mot_Enc1.pin4, DC_Mot_Enc2.pin4, Part2.GND, DC_Mot_Enc5.pin4, U1.H1, Part1.GND, J1.gnd
  5V: MD03A1.+5V_(IN), MD03A2.+5V_(IN), DC_Mot_Enc1.pin5, DC_Mot_Enc2.pin5, DC_Mot_Enc5.pin5, U1.H2, Part1.5V, J1.vcc
  N4: MD03A1.2PWM, Part1.D4_PWM
  N5: MD03A1.2INb#142, Part1.D5_PWM
  N6: MD03A1.2INb#143, Part1.D6_PWM
  N7: MD03A1.OUT_1A, DC_Mot_Enc2.pin1
  N8: MD03A1.OUT_1B, DC_Mot_Enc2.pin2
  N9: MD03A1.OUT_2A, DC_Mot_Enc1.pin1
  N10: MD03A1.OUT_2B, DC_Mot_Enc1.pin2
  VIN: MD03A1.VIN, MD03A2.VIN, VCC1.+
  N11: MD03A1.GND#151, MD03A2.GND#151, VCC1.-
  N12: MD03A2.2PWM, Part1.D42
  N13: MD03A2.2INb#142, Part1.D44
  N14: MD03A2.2INb#143, Part1.D43
  N15: MD03A2.OUT_1A, DC_Mot_Enc5.pin1
  N16: MD03A2.OUT_1B, DC_Mot_Enc5.pin2
  N17: DC_Mot_Enc1.pin3, Part1.D21/SCL
  N18: DC_Mot_Enc1.pin6, Part1.D20/SDA, Part1.SDA
  N19: DC_Mot_Enc2.pin3, Part1.D19/RX1
  N20: DC_Mot_Enc2.pin6, Part1.D18/TX1
  VCC: Part2.VCC, Part1.3V3
  N21: Part2.CE, Part1.D8_PWM
  N22: Part2.CS, Part1.D53
  N23: Part2.SCK, Part1.D52
  N24: Part2.MOSI, Part1.D51
  N25: Part2.MISO, Part1.D50
  N26: DC_Mot_Enc5.pin3, Part1.D2_PWM
  N27: DC_Mot_Enc5.pin6, Part1.D3_PWM
  N28: U1.A1, Part1.A0
  N29: Part1.D46, J1.pulse
