# Fritzing sketch stepper (saved by Fritzing 0.9.3b)
circuit board: 8.46667cm x 5.64444cm
breadboards: 1

parts:
  IC2 = H-Bridge [package=THT]
  M1 = Stepper Motor - Bipolar
  VCC1 = Battery block 9V
  Part2 = Arduino Mega ADK (Rev3)

nets:
  N1: IC2.1_2EN, IC2.3_4EN, IC2.VCC1, Part2.5V
  N2: IC2.1A, Part2.D23
  N3: IC2.1Y, M1.B
  GND1: IC2.GND1, IC2.GND2, IC2.GND3, IC2.GND4, VCC1.-, Part2.GND
  N4: IC2.2Y, M1.A
  N5: IC2.2A, Part2.D22
  N6: IC2.3A, Part2.D24
  N7: IC2.3Y, M1.C
  N8: IC2.4Y, M1.D
  N9: IC2.4A, Part2.D25
